# Fritzing sketch basic speaker test (saved by Fritzing 0.9.3b)

parts:
  Part1 = Arduino Uno (Rev3) - ICSP
  SP1 = SPEAKER [package=pcb_mount_speaker]
  R1 = Resistor [tolerance=±5% resistance=100 package="1206 [SMD]"]

nets:
  N1: Part1.D8, R1.Pin_1
  N2: Part1.GND, SP1.+
  N3: SP1.-, R1.Pin_0
