# Fritzing sketch lm386-Diagram (saved by Fritzing 0.9.3b)
breadboards: 1

parts:
  U1 = LM386 [package=dip08]
  R1 = Resistor [tolerance=±5% resistance=1k package=THT]
  C1 = Electrolytic Capacitor [capacitance=10µF package="100 mil [THT, electrolytic]"]
  C3 = Electrolytic Capacitor [capacitance=0.1mF package="100 mil [THT, electrolytic]"]
  C4 = Electrolytic Capacitor [capacitance=0.1mF package="100 mil [THT, electrolytic]"]
  C5 = Electrolytic Capacitor [capacitance=1mF package="200 mil [THT, electrolytic]"]
  C6 = Ceramic Capacitor [capacitance=0.1µF package="100 mil [THT, multilayer]"]
  Part1 = Arduino Nano (Rev3.0) (ICSP)
  Part2 = MicroSD Card Module
  SP1 = SPEAKER [package=pcb_mount_speaker]
  S1 = Pushbutton [package="[THT]"]
  R2 = Resistor [tolerance=±5% resistance=1k package=THT]

nets:
  N1: U1.GAIN, C1.-, C1.+
  GND: U1.-IN, U1.V-, R1.Pin_1, C3.-, C4.-, C6.0, Part1.GND, Part2.GND, SP1.+, R2.Pin_0
  N2: U1.+IN, R1.Pin_0, Part1.D9
  N3: U1.OUT, C5.+
  5V: U1.V+, C3.+, Part1.5V, Part2.VCC, S1.Pin_1, S1.Pin_2
  N4: U1.BP, C4.+
  N5: C5.-, C6.1, SP1.-
  N6: Part1.D2, S1.Pin_3, S1.Pin_4, R2.Pin_1
  N7: Part1.D4, Part2.CS
  N8: Part1.D11/MOSI, Part2.MOSI
  N9: Part1.D12/MISO, Part2.MISO
  N10: Part1.D13/SCK, Part2.SCK
