# Fritzing sketch lm386-Diagram (saved by Fritzing 0.9.3b)
breadboards: 1

parts:
  Part1 = Arduino Uno (Rev3) - ICSP
  Part2 = MicroSD Card Module
  U1 = LM386 [package=dip08]
  R1 = Resistor [tolerance=±5% resistance=1k package=THT]
  C1 = Electrolytic Capacitor [capacitance=10µF package="100 mil [THT, electrolytic]"]
  SP1 = SPEAKER [package=pcb_mount_speaker]
  C3 = Electrolytic Capacitor [capacitance=0.1mF package="100 mil [THT, electrolytic]"]
  C4 = Electrolytic Capacitor [capacitance=0.1mF package="100 mil [THT, electrolytic]"]
  C5 = Electrolytic Capacitor [capacitance=1mF package="200 mil [THT, electrolytic]"]
  C6 = Ceramic Capacitor [capacitance=0.1µF package="100 mil [THT, multilayer]"]

nets:
  N1: Part1.ICSP_MOSI, Part1.D11_PWM/MOSI, Part2.MISO
  N2: Part1.D9_PWM, U1.+IN, R1.Pin_1
  N3: Part1.D12/MISO, Part2.MOSI
  N4: Part1.D13/SCK, Part2.SCK
  N5: Part1.D4, Part2.CS
  N6: Part2.GND, U1.-IN, U1.V-, R1.Pin_0, SP1.+, C3.-, C4.-, C6.0
  N7: Part2.VCC, U1.V+, C3.+
  N8: U1.GAIN, C1.-, C1.+
  N9: U1.OUT, C5.+
  N10: U1.BP, C4.+
  N11: SP1.-, C5.-, C6.1
