# Fritzing sketch diagram (saved by Fritzing 0.9.3b)
breadboards: 1

parts:
  Part1 = Arduino Uno (Rev3)
  S1 = Pushbutton [package="[THT]"]
  Part2 = MicroSD Card Module
  R1 = Resistor [tolerance=±5% resistance=220 package=THT]

nets:
  N1: Part1.D8, Part2.CS
  N2: Part1.D11_PWM/MOSI, Part2.MOSI
  N3: Part1.D12/MISO, Part2.MISO
  N4: Part1.D13/SCK, Part2.SCK
  GND: Part1.GND, Part2.GND, R1.Pin_0
  N5: Part1.D4, S1.Pin_3, S1.Pin_4, R1.Pin_1
  5V: Part1.5V, S1.Pin_1, S1.Pin_2, Part2.VCC
